# Fritzing sketch robotwirediagram (saved by Fritzing 0.9.3b)
stripboards: 1

parts:
  IC1 = L293D [package=THT]
  J1 = Screw terminal - 2 pins [package=THT]
  C1 = Ceramic Capacitor [capacitance=100nF package="100 mil [THT, multilayer]"]
  J2 = Camdenboss CTB0158-2 [part_number=CTB0158-2 package=THT]
  C2 = Ceramic Capacitor [capacitance="100 nF" package="1206 [SMD, multilayer]"]
  Raspberry_Pi_1 = Raspberry Pi 3 [part_number=RPI-3-V1.2]
  M1 = DC Motor
  M2 = DC Motor
  J3 = Camdenboss CTB0158-2 [part_number=CTB0158-2 package=THT]
  VCC1 = Battery block 9V

nets:
  N1: IC1.Enable_1, Raspberry_Pi_1.GIPO25
  N2: IC1.In_1, Raspberry_Pi_1.GIPO24
  N3: IC1.0V, J2.pin1, M1.pin_1, J3.pin2
  N4: IC1.Out_2_(_Controlled_by_Enable_1_), J2.pin2
  N5: IC1.In_2, Raspberry_Pi_1.GIPO23
  N6: IC1.+Vmotor, J1.pin1, C2.0, C2.1, VCC1.+
  N7: IC1.Enable_2, Raspberry_Pi_1.GIPO17
  N8: IC1.In_3, Raspberry_Pi_1.GIPO22
  N9: IC1.Out_3_(_Controlled_by_Enable_2_), M1.pin_2, J3.pin1
  N10: IC1.Out_4_(_Controlled_by_Enable_2_), Raspberry_Pi_1.GIPO27
  N11: IC1.+V, C1.1, Raspberry_Pi_1.5V
  N12: J1.pin2, VCC1.-
  N13: C1.0, Raspberry_Pi_1.GND
  N14: J2.terminal_1, M2.pin_2
  N15: J2.terminal_2, M2.pin_1
